# Fritzing sketch weather_station (saved by Fritzing 0.9.3b)
breadboards: 1

parts:
  WeMos_D1_Mini1 = WeMos D1 Mini
  RHT1 = Humidity and Temperature Sensor RHT03
  R1 = Resistor [tolerance=±5% resistance=4.7k package="0402 [SMD]"]

nets:
  5V: WeMos_D1_Mini1.5V, RHT1.Vcc, R1.Pin_1
  N1: WeMos_D1_Mini1.D0, RHT1.Data-signal
  N2: WeMos_D1_Mini1.G, RHT1.GND_2
